// Digital circuit Seta.dig as structural Verilog
module Seta (
  input  clk
);

  wire Botao_Seta_Direita_out, Botao_Seta_Esquerda_out, resposta_1_seta, resposta_2_seta;

  LED Seta_Direita (.in(resposta_1_seta));
  resposta resposta_1 (.CLK(clk), .Btn_Seta(Botao_Seta_Esquerda_out), .seta(resposta_1_seta));
  DipSwitch Botao_Seta_Esquerda (.out(Botao_Seta_Esquerda_out));
  DipSwitch Botao_Seta_Direita (.out(Botao_Seta_Direita_out));
  resposta resposta_2 (.CLK(clk), .Btn_Seta(Botao_Seta_Direita_out), .seta(resposta_2_seta));
  LED Seta_Direita_2 (.in(resposta_2_seta));

  // Notes on the sheet:
  //   Esse eh o circuito principal que sera usado para testes. Nao edite.
endmodule
