// Digital circuit resposta.dig as structural Verilog
module resposta (
  input  CLK,
  input  Btn_Seta,
  output seta
);

  wire and_1_out, and_2_out, and_3_out, and_4_out, and_5_out, and_6_out, and_7_out, and_8_out, and_9_out,
       and_10_out, and_11_out, d_ff_1_q, d_ff_2_q, d_ff_3_q, jk_ff_1_q, or_1_out, or_2_out, or_3_out,
       xor_1_out;

  and and_1 (and_1_out, ~d_ff_1_q, d_ff_3_q, jk_ff_1_q);  // And
  and and_2 (and_2_out, ~d_ff_1_q, d_ff_2_q, jk_ff_1_q);  // And
  and and_3 (and_3_out, d_ff_1_q, d_ff_3_q, ~jk_ff_1_q);  // And
  and and_4 (and_4_out, d_ff_1_q, d_ff_2_q, ~jk_ff_1_q);  // And
  and and_5 (and_5_out, ~d_ff_3_q, jk_ff_1_q);  // And
  JK_FF jk_ff_1 (.J(Btn_Seta), .C(xor_1_out), .K(d_ff_3_q), .Q(jk_ff_1_q));  // open: nQ
  xor xor_1 (xor_1_out, Btn_Seta, d_ff_3_q);
  and and_6 (and_6_out, ~jk_ff_1_q, d_ff_3_q, ~d_ff_2_q);  // And
  or or_1 (or_1_out, and_8_out, and_6_out);
  or or_2 (or_2_out, and_1_out, and_2_out, and_3_out, and_4_out);
  or or_3 (or_3_out, and_5_out, and_7_out, and_9_out);
  and and_7 (and_7_out, d_ff_1_q, ~d_ff_3_q);  // And
  and and_8 (and_8_out, ~jk_ff_1_q, ~d_ff_3_q, d_ff_1_q);  // And
  and and_9 (and_9_out, d_ff_1_q, jk_ff_1_q);
  D_FF d_ff_1 (.D(or_1_out), .C(CLK), .Q(d_ff_1_q));  // open: nQ
  D_FF d_ff_2 (.D(or_2_out), .C(CLK), .Q(d_ff_2_q));  // open: nQ
  D_FF d_ff_3 (.D(or_3_out), .C(CLK), .Q(d_ff_3_q));  // open: nQ
  and and_10 (and_10_out, d_ff_2_q, ~d_ff_3_q);  // And
  and and_11 (and_11_out, d_ff_1_q, ~d_ff_3_q);  // And
  or or_4 (seta, and_10_out, and_11_out);
endmodule
